# Fritzing sketch plantMonitorFritz (saved by Fritzing 1.0.4)
breadboards: 2

parts:
  A1 = Particle - Photon2
  Part1 = MQ-131 breakout
  OLED_I2C1 = OLED 128x64 I2C Monochrome Display
  M1 = BMP280
  Part2 = 12 NeoPixel Ring [part_number=1643]
  Part3 = 12 NeoPixel Ring [part_number=1643]
  A2 = USB A power source
  Relay1 = Relay - 6 pins [package="DIP (Dual Inline) [THT]"]
  Relay2 = Relay - 6 pins [package="DIP (Dual Inline) [THT]"]
  WATER_PUMP1 = water pump/motor  # not connected
  M2 = seeed grove atomizer v1.0
  Q1 = PNP-Transistor [package="TO92 [THT]"]
  Q2 = PNP-Transistor [package="TO92 [THT]"]
  R2 = Resistor [tolerance=±5% resistance=220 package="0402 [SMD]"]
  R3 = Resistor [tolerance=±5% resistance=2.2k package="2010 [SMD]"]
  R4 = Resistor [tolerance=±5% resistance=2.2k package="2010 [SMD]"]
  R5 = Resistor [tolerance=±5% resistance=220 package="0402 [SMD]"]
  S4 = SWITCH-MOMENTARY-2 [package=tactile-switch-1101ne]
  S5 = SWITCH-MOMENTARY-2 [package=tactile-switch-1101ne]
  SENS1 = SoilWatch 10

nets (from the schematic view):
  VCC: A1.Pin_2, A1.Pin_31, Part1.VCC, OLED_I2C1.VDD, M1.VIN, SENS1.VCC
  GND: A1.Pin_4, A1.Pin_30, Part1.GND, OLED_I2C1.GND, M1.GND, Part2.GND, Part3.GND, Relay1.GND, Relay2.GND, M2.GND, R3.Pin_1, R4.Pin_1, S4.2, S5.1
  N1: A1.Pin_5, Part1.DO
  N2: A1.Pin_6, SENS1.OUT
  N3: A1.Pin_14, S4.1
  N4: A1.Pin_17, OLED_I2C1.SDA, M1.SDA
  N5: A1.Pin_18, OLED_I2C1.SCK, M1.SCL
  N6: A1.Pin_19, Part2.IN
  N7: A1.Pin_21, Q2.B, R4.Pin_0
  N8: A1.Pin_22, Q1.B, R3.Pin_0
  N9: A1.Pin_24, S5.2
  VCC_2: A1.Pin_26, Relay1.VCC, Relay2.VCC
  N10: Part2.OUT, Part3.IN
  VDD: Part2.VDD, Part3.VDD, A2.Pin_1, Relay1.ON, Relay2.ON, R2.Pin_0, R5.Pin_0
  N11: A2.Pin_2, Q1.C, Q2.C, SENS1.GND
  N12: Relay1.IN, Q2.E, R2.Pin_1
  N13: Relay2.IN, Q1.E, R5.Pin_1
  N14: Relay2.COM, M2.VCC

notes:
  5V Wall USB External Power Supply with Common Ground
  IC2
  Common Ground
  ~~~~~~~~~~~~~~~~~~~~~~~~~~~~~~~~~~~~~~~~
  ~~~~~~~~~~~ Plant Habitat Monitor ~~~~~~~~~~
  ~~~~~~~~~~~~~~~~~~~~~~~~~~~~~~~~~~~~~~~~
  Hardware
  _____________________________________________________
  Photon 2: OS 5.8.0 , best for NeoPixels
  BME280: I2C 0x76
  OLE: I2C SSD1306 128x64, 0x3C
  Soil sensor: A0, capacitive
  Air quality: A1, Grove MP-503
  Pump relay : D4, Songle SRD-05DC-SLC
  Mist relay : D5, SongleSRD-05DC-SLC
  NeoPixels : D2, WS2812B, 2x12 rings
  Mode momentary button: D9
  (short press = next OLED page, long press = AUTO/MANUAL toggle)
  Mist momentary button: D7
  (short = mist burst, long = pump cycle)
  _____________________________________________________
  neoPixel Rings connected back-to-back
  Short: next OLED page
  Long: Auto/Manual Toggle
  Short: mist
  Long: pump cycle
  Note: swapped out relays for MOSFETS, added circuit protective measures:
  IRLZ44Ns (220 ohm from pin to Gate, 10K ohm Gate to Source, flyback diodes across pump and mister), 1000uf cap across neoPixels, 330 ohm pull-ups from IC2

custom parts:
  Particle - Photon2: The Photon 2 is a microcontroller and Wi-Fi networking developed by particle. Features: 802.11a/b/g/n Wi-Fi, 2.4 GHz and 5 GHz Integrated PCB antenna Integrated U.FL connector for external antenna Integrated RF switch BLE 5 using same antenna as Wi-Fi Realtek RTL8721DM MCU ARM Cortex M33 CPU, 200 MHz 2048 KB (2 MB) user application maximum size 3072 KB (3 MB) of RAM available to user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
  MQ-131 breakout: SKU: 101282
  BMP280: Temperature Humidity Barometric presure Sensor, I2C
  12 NeoPixel Ring: 12 ultra bright smart LED NeoPixels are arranged in a circle with 1.5" (37mm) outer diameter. The rings are 'chainable' - connect the output pin of one to the input pin of another. Use only one microcontroller pin to control as many as you can chain together! Each LED is addressable as the driver chip is inside the LED. Each one has ~18mA constant current drive so the color will be very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
  USB A power source: USB A power source.
  Relay - 6 pins: A DIP stand-in part for whatever IC you want. With 6 pins on a 900mil dual inline package (DIP) footprint.
  water pump/motor: WATER PUMP BY ARDUBLOCKTR
  seeed grove atomizer v1.0: Grove - Water Atomization is a perfect module for you to quickly DIY a humidifier with Arduino. You can also develop more advanced and interesting projects with digital scent technology and any other situations in which atomization required.
  SoilWatch 10: SoilWatch 10 - Capacitive soil moisture sensor
